# Fritzing sketch sketch (saved by Fritzing 0.9.3b)
breadboards: 1

parts:
  S1 = H-Bridge with L298N
  Part1 = Arduino Pro Mini v13
  M1 = DC Motor
  M2 = DC Motor
  Part2 = LilyPad LED
  Q1 = NPN-Transistor [package="SOT-23 [SMD]"]
  R1 = Resistor [tolerance=±5% resistance=220 package=THT]
  J1 = Infrared Proximity Sensor
  J2 = Infrared Proximity Sensor
  J3 = Power Jack [package=power_jack_combo]
  J4 = Power Jack [package=power_jack_combo]

nets:
  N1: S1.12V, J3.PWR
  GND: S1.GND, Q1.2, J1.GND, J2.GND, J3.GND, J4.GND
  N2: S1.ENA, S1.IN1, S1.IN2, Part1.A4, Part1.A5, Part1.A3, Part1.A2, Part1.D5_PWM
  N3: S1.ENB, Part1.D6_PWM
  N4: S1.M1-01, M2.pin_2
  N5: S1.M1-02, M2.pin_1
  N6: S1.M2-01, M1.pin_2
  N7: S1.M2-02, M1.pin_1
  N8: Part1.A1, J2.Vout
  N9: Part1.A0, J1.Vout
  N10: Part1.D3_PWM, Q1.0, R1.Pin_0, R1.Pin_1
  VCC: Part2.+, J1.Vcc, J2.Vcc, J4.PWR
  N11: Part2.-, Q1.1

custom parts:
  H-Bridge with L298N: h-bridge
